// Logisim project MyMicroProcessor.circ as structural Verilog
module main (
);

  Processor_V2 processor_v2_1 ();  // open: IN01_8, IN01_4, IN01_2, IN01_1, IN02_8, IN02_4, IN02_2, IN02_1, IN03_8, IN03_4, IN03_2, IN03_1, IN04_8, IN04_4, IN04_2, IN04_1, IN05_8, IN05_4, IN05_2, IN05_1, IN06_8, IN06_4, IN06_2, IN06_1, IN07_8, IN07_4, IN07_2, IN07_1, IN08_8, IN08_4, IN08_2, IN08_1, RESET, Inc_Program_Address, Decrease_Program_Address, Reset_Program_Address, Write_Program_Data, Program, PD8, PD4, PD2, PD1, OUT01_1, OUT01_2, OUT01_4, OUT01_8, OUT02_1, OUT02_2, OUT02_4, OUT02_8, OUT03_1, OUT03_2, OUT03_4, OUT03_8, OUT04_1, OUT04_2, OUT04_4, OUT04_8, OUT05_1, OUT05_2, OUT05_4, OUT05_8, OUT06_1, OUT06_2, OUT06_4, OUT06_8, OUT07_1, OUT07_2, OUT07_4, OUT07_8, OUT08_1, OUT08_2, OUT08_4, OUT08_8
endmodule

module Processor (
  input  RESET,
  input  Increase_Program_Address,
  input  Decrease_Program_Address,
  input  Reset_Program_Address,
  input  Write_Program_Data,
  input  Program,
  input  [3:0] Program_Data
);

  wire and_1_out, and_4_out, clock_1_out, instruction_decoder_1_p1, instruction_decoder_1_p2,
       instruction_decoder_1_p3, instruction_decoder_1_p4, instruction_decoder_1_p5,
       instruction_decoder_1_p6, instruction_decoder_1_p7, instruction_decoder_1_p8,
       instruction_decoder_1_p9, instruction_decoder_1_p10, instruction_decoder_1_p11,
       instruction_decoder_1_p12, instruction_decoder_1_p13, instruction_decoder_1_p14,
       instruction_decoder_1_p15, instruction_decoder_1_p16, instruction_decoder_1_p17, or_1_out, or_2_out,
       or_3_out, Program_IP_REG_p3, Program_IP_REG_p5, undriven, undriven_2, undriven_3, undriven_4,
       undriven_5, undriven_6, undriven_7, undriven_8, xor_1_out;
  wire [1:0] alu_1_zero_flag;
  wire [3:0] alu_1_q, Instruction_Register_q, pull_resistor_4_node, pull_resistor_6_node,
       pull_resistor_10_node, ram_1_data, WREG_q, \µ_instruction_counter_1_q ;
  wire [11:0] register_12b_1_q;

  Pull_Resistor pull_resistor_1 (.node(pull_resistor_4_node[1]));
  Pull_Resistor pull_resistor_2 (.node(pull_resistor_4_node[2]));
  Pull_Resistor pull_resistor_3 (.node(pull_resistor_10_node[3]));
  Pull_Resistor pull_resistor_4 (.node(pull_resistor_4_node[0]));
  Pull_Resistor pull_resistor_5 (.node(pull_resistor_4_node[3]));
  Hex_Digit_Display hex_digit_display_1 (.value(pull_resistor_4_node));  // open: dp
  Pull_Resistor pull_resistor_6 (.node(pull_resistor_6_node[0]));
  Pull_Resistor pull_resistor_7 (.node(pull_resistor_10_node[2]));
  Pull_Resistor pull_resistor_8 (.node(pull_resistor_6_node[3]));
  Pull_Resistor pull_resistor_9 (.node(pull_resistor_10_node[1]));
  Pull_Resistor pull_resistor_10 (.node(pull_resistor_10_node[0]));
  Pull_Resistor pull_resistor_11 (.node(pull_resistor_6_node[2]));
  Pull_Resistor pull_resistor_12 (.node(pull_resistor_6_node[1]));
  and and_1 (and_1_out, Increase_Program_Address, Program);
  Hex_Digit_Display hex_digit_display_2 (.value(pull_resistor_6_node));  // open: dp
  Hex_Digit_Display hex_digit_display_3 (.value(pull_resistor_10_node));  // open: dp
  // IP_Register Program_IP_REG: pin names not known; wires that end beside it: {pull_resistor_4_node, pull_resistor_10_node, pull_resistor_6_node}, and_1_out, Program_IP_REG_p3, Program, Program_IP_REG_p5
  IP_Register IP_REG (
    .SAVE(instruction_decoder_1_p15), .DATA(register_12b_1_q), .INC(instruction_decoder_1_p4),
    .Read(instruction_decoder_1_p1),
    .ADRESS_FOR_RAM({pull_resistor_4_node, pull_resistor_10_node, pull_resistor_6_node}), .RESET(RESET));  // open: DEC
  and and_2 (Program_IP_REG_p3, Decrease_Program_Address, Program);
  register_12b register_12b_1 (
    .Data({pull_resistor_4_node, pull_resistor_10_node, pull_resistor_6_node}),
    .Write(instruction_decoder_1_p14), .Read(1'b1), .Q(register_12b_1_q));  // open: Clear
  or or_1 (or_1_out, instruction_decoder_1_p13, and_4_out, instruction_decoder_1_p2);
  and and_3 (Program_IP_REG_p5, Reset_Program_Address, Program);
  RAM #(.addrWidth(12), .dataWidth(4), .bus("asynch")) ram_1 (
    .addr({pull_resistor_4_node, pull_resistor_10_node, pull_resistor_6_node}), .data(ram_1_data),
    .sel(or_1_out), .ld(instruction_decoder_1_p2), .clr(1'b0));
  and and_4 (and_4_out, Write_Program_Data, Program);
  register Instruction_Param_3 (
    .Data(ram_1_data), .Write(instruction_decoder_1_p8), .Read(instruction_decoder_1_p11),
    .Q(pull_resistor_6_node));  // open: Clear
  register Instruction_Param_2 (
    .Data(ram_1_data), .Write(instruction_decoder_1_p6), .Read(instruction_decoder_1_p10),
    .Q(pull_resistor_10_node));  // open: Clear
  register Intruction_Param_1 (
    .Data(ram_1_data), .Write(instruction_decoder_1_p5), .Read(instruction_decoder_1_p9),
    .Q(pull_resistor_4_node));  // open: Clear
  Hex_Digit_Display hex_digit_display_4 (.value(ram_1_data));  // open: dp
  outputter outputter_1 (.In(Program_Data), .Read(Program), .Out(ram_1_data));
  Pull_Resistor pull_resistor_13 (.node(ram_1_data[1]));
  Pull_Resistor pull_resistor_14 (.node(ram_1_data[3]));
  Pull_Resistor pull_resistor_15 (.node(ram_1_data[2]));
  Pull_Resistor pull_resistor_16 (.node(ram_1_data[0]));
  outputter MOVWR (.In(WREG_q), .Read(instruction_decoder_1_p16), .Out(ram_1_data));
  register Instruction_Register (
    .Data(ram_1_data), .Write(instruction_decoder_1_p3), .Read(1'b1), .Q(Instruction_Register_q));  // open: Clear
  register WREG (
    .Data(ram_1_data), .Write(instruction_decoder_1_p12), .Read(instruction_decoder_1_p17), .Q(WREG_q));  // open: Clear
  Hex_Digit_Display hex_digit_display_5 (.value(Instruction_Register_q));  // open: dp
  ALU alu_1 (
    .A(WREG_q), .B(ram_1_data), .Subtract(undriven), .Nor(undriven_2), .Xor(undriven_3), .Nand(undriven_4),
    .Add(undriven_5), .Carry_Flag(alu_1_zero_flag[1]), .Zero_Flag(alu_1_zero_flag[0]), .Q(alu_1_q));
  register Flags (.Data({2'b00, alu_1_zero_flag}), .Write(undriven_6), .Read(1'b1));  // open: Clear, Q
  register Buffer (.Data(alu_1_q), .Write(undriven_7), .Read(undriven_8), .Q(ram_1_data));  // open: Clear
  // instruction_decoder instruction_decoder_1: pin names not known; wires that end beside it: instruction_decoder_1_p1, instruction_decoder_1_p2, instruction_decoder_1_p3, instruction_decoder_1_p4, instruction_decoder_1_p5, instruction_decoder_1_p6, instruction_decoder_1_p7, instruction_decoder_1_p8, instruction_decoder_1_p9, instruction_decoder_1_p10, instruction_decoder_1_p11, instruction_decoder_1_p12, instruction_decoder_1_p13, instruction_decoder_1_p14, instruction_decoder_1_p15, instruction_decoder_1_p16, instruction_decoder_1_p17
  Hex_Digit_Display hex_digit_display_6 (.value(\µ_instruction_counter_1_q ));  // open: dp
  \µ_Instruction_Counter  \u_µ_instruction_counter_1  (
    .Increase(or_2_out), .Clear(or_3_out), .Q(\µ_instruction_counter_1_q ));
  or or_2 (or_2_out, clock_1_out, xor_1_out);
  or or_3 (or_3_out, instruction_decoder_1_p7, RESET);
  buf xor_1 (xor_1_out, RESET);  // XOR_Gate
  Clock clock_1 (.out(clock_1_out));

  // Notes on the sheet:
  //   Reset_Program_Address: pull=down
  //   Program: pull=down
  //   Decrease_Program_Address: pull=down
  //   RESET: pull=down
  //   Write_Program_Data: pull=down
  //   Increase_Program_Address: pull=down
  //   Program_Data: pull=down
  //   0001 XXXX XXXX XXXX - MOVRW
  //   0010 XXXX XXXX XXXX - MOVWR
  //   0101 XXXX XXXX XXXX - JMP
  //   0000 - NOP
  //   0011 XXXX - MOVWO
  //   0100 XXXX - MOVIW
endmodule

module ALU (
  input  [3:0] A,
  input  Subtract,
  input  Add,
  input  [3:0] B,
  input  Nor,
  input  Xor,
  input  Nand,
  output [3:0] Q,
  output Carry_Flag,
  output Zero_Flag
);

  wire or_1_out;
  wire [3:0] adder_1_out, nand_1_out, nor_1_out, outputter_5_out, xor_1_out, xor_2_out;

  assign xor_1_out = B ^ {4{Subtract}};  // XOR_Gate xor_1, 4 bits wide
  Adder #(.width(4)) adder_1 (.a(A), .b(xor_1_out), .out(adder_1_out), .cin(Subtract), .cout(Carry_Flag));
  assign nor_1_out = ~(A | B);  // NOR_Gate nor_1, 4 bits wide
  assign xor_2_out = A ^ B;  // XOR_Gate xor_2, 4 bits wide
  assign nand_1_out = ~(A & B);  // NAND_Gate nand_1, 4 bits wide
  or or_1 (or_1_out, Subtract, Add);
  outputter outputter_1 (.In(adder_1_out), .Read(or_1_out), .Out(Q));
  outputter outputter_2 (.In(nor_1_out), .Read(Nor), .Out(Q));
  outputter outputter_3 (.In(xor_2_out), .Read(Xor), .Out(Q));
  outputter outputter_4 (.In(nand_1_out), .Read(Nand), .Out(Q));
  outputter outputter_5 (.In(Q), .Read(1'b1), .Out(outputter_5_out));
  and and_1 (Zero_Flag, ~outputter_5_out[3], ~outputter_5_out[2], ~outputter_5_out[1], ~outputter_5_out[0]);  // AND_Gate

  // Notes on the sheet:
  //   Nand: pull=down
  //   Subtract: pull=down
  //   Xor: pull=down
  //   A: pull=down
  //   B: pull=down
  //   Add: pull=down
  //   Nor: pull=down
endmodule

// REG
module register (
  input  Read,
  input  [3:0] Data,
  input  Write,
  input  Clear,
  output [3:0] Q
);

  wire [3:0] register_1_q;

  Register #(.width(4), .trigger("high")) register_1 (.D(Data), .en(1'b1), .Q(register_1_q), .clk(Write), .clr(Clear));
  outputter outputter_1 (.In(register_1_q), .Read(Read), .Out(Q));

  // Notes on the sheet:
  //   Write: pull=down
  //   Data: pull=down
  //   Clear: pull=down
  //   Read: pull=down
endmodule

module register_12b (
  input  [11:0] Data,
  input  Write,
  input  Clear,
  input  Read,
  output [11:0] Q
);

  wire [11:0] register_1_q;

  Register #(.width(12), .trigger("high")) register_1 (.D(Data), .en(1'b1), .Q(register_1_q), .clk(Write), .clr(Clear));
  outputter outputter_1 (.In(register_1_q[3:0]), .Read(Read), .Out(Q[3:0]));
  outputter outputter_2 (.In(register_1_q[7:4]), .Read(Read), .Out(Q[7:4]));
  outputter outputter_3 (.In(register_1_q[11:8]), .Read(Read), .Out(Q[11:8]));

  // Notes on the sheet:
  //   Data: pull=down
  //   Write: pull=down
  //   Read: pull=down
  //   Clear: pull=down
endmodule

module outputter (
  input  Read,
  input  [3:0] In,
  output [3:0] Out
);

  Transistor #(.\type ("n")) transistor_1 (.in(In[0]), .out(Out[0]), .gate(Read));
  Transistor #(.\type ("n")) transistor_2 (.in(In[1]), .out(Out[1]), .gate(Read));
  Transistor #(.\type ("n")) transistor_3 (.in(In[2]), .out(Out[2]), .gate(Read));
  Transistor #(.\type ("n")) transistor_4 (.in(In[3]), .out(Out[3]), .gate(Read));

  // Notes on the sheet:
  //   Read: pull=down
  //   In: pull=down
endmodule

// CNTR
module IP_Register (
  input  SAVE,
  input  [11:0] DATA,
  input  INC,
  input  DEC,
  input  RESET,
  input  Read,
  output [11:0] ADRESS_FOR_RAM
);

  wire or_1_out, or_2_out, or_3_out;
  wire [11:0] counter_1_q;

  or or_1 (or_1_out, INC, DEC, SAVE);
  or or_2 (or_2_out, DEC, SAVE);
  or or_3 (or_3_out, INC, DEC);
  Counter #(.width(12), .max('hfff)) counter_1 (
    .load(or_2_out), .D(DATA), .count(or_3_out), .Q(counter_1_q), .clk(or_1_out), .clr(RESET));  // open: carry
  outputter outputter_1 (.In(counter_1_q[3:0]), .Read(Read), .Out(ADRESS_FOR_RAM[3:0]));
  outputter outputter_2 (.In(counter_1_q[7:4]), .Read(Read), .Out(ADRESS_FOR_RAM[7:4]));
  outputter outputter_3 (.In(counter_1_q[11:8]), .Read(Read), .Out(ADRESS_FOR_RAM[11:8]));

  // Notes on the sheet:
  //   DATA: pull=down
  //   DEC: pull=down
  //   Read: pull=down
  //   SAVE: pull=down
  //   INC: pull=down
  //   RESET: pull=down
endmodule

module \µ_Instruction_Counter  (
  input  Increase,
  input  Clear,
  output [3:0] Q
);

  wire not_1_out;

  not not_1 (not_1_out, Increase);
  Counter #(.width(4), .max('hf)) counter_1 (
    .count(not_1_out), .Q(Q), .clk(not_1_out), .clr(Clear));  // open: load, D, carry

  // Notes on the sheet:
  //   Q: pull=down
  //   Clear: pull=down
  //   Increase: pull=down
endmodule

module _4b_decoder (
  input  [3:0] data,
  output out_2,
  output out_3,
  output out_4,
  output out_5,
  output out_6,
  output out_7,
  output out_8,
  output out_9,
  output out_10,
  output out_11,
  output out_12,
  output out_13,
  output out_14,
  output out_15,
  output out_16,
  output out_17
);

  and and_1 (out_2, ~data[3], ~data[2], ~data[1], ~data[0]);  // AND_Gate
  and and_2 (out_3, ~data[3], ~data[2], ~data[1], data[0]);  // AND_Gate
  and and_3 (out_4, ~data[3], ~data[2], data[1], ~data[0]);  // AND_Gate
  and and_4 (out_5, ~data[3], ~data[2], data[1], data[0]);  // AND_Gate
  and and_5 (out_6, ~data[3], data[2], ~data[1], ~data[0]);  // AND_Gate
  and and_6 (out_7, ~data[3], data[2], ~data[1], data[0]);  // AND_Gate
  and and_7 (out_8, ~data[3], data[2], data[1], ~data[0]);  // AND_Gate
  and and_8 (out_9, ~data[3], data[2], data[1], data[0]);  // AND_Gate
  and and_9 (out_10, data[3], ~data[2], ~data[1], ~data[0]);  // AND_Gate
  and and_10 (out_11, data[3], ~data[2], ~data[1], data[0]);  // AND_Gate
  and and_11 (out_12, data[3], ~data[2], data[1], ~data[0]);  // AND_Gate
  and and_12 (out_13, data[3], ~data[2], data[1], data[0]);  // AND_Gate
  and and_13 (out_14, data[3], data[2], ~data[1], ~data[0]);  // AND_Gate
  and and_14 (out_15, data[3], data[2], ~data[1], data[0]);  // AND_Gate
  and and_15 (out_16, data[3], data[2], data[1], ~data[0]);  // AND_Gate
  and and_16 (out_17, data[3], data[2], data[1], data[0]);

  // Notes on the sheet:
  //   out_2: pull=down
  //   out_3: pull=down
  //   out_6: pull=down
  //   out_14: pull=down
  //   out_4: pull=down
  //   out_11: pull=down
  //   out_10: pull=down
  //   out_16: pull=down
  //   out_13: pull=down
  //   out_5: pull=down
  //   out_12: pull=down
  //   out_7: pull=down
  //   data: pull=down
  //   out_17: pull=down
  //   out_9: pull=down
  //   out_8: pull=down
  //   out_15: pull=down
endmodule

// INSTRUCTION DEC
module instruction_decoder (
  input  [3:0] \µ_Instruction_Counter ,
  input  Clock,
  input  [3:0] Instruction,
  output Memory_Read,
  output IP_Increase,
  output \µIC_Clear ,
  output IParam1_Write,
  output IParam3_Write,
  output IParam2_Read,
  output WREG_Write,
  output IP_Read,
  output Instruction_reg__Write,
  output IParam2_Write,
  output IParam1_Read,
  output IParam3_Read,
  output Memory_Write
);

  wire and_4_out, n4b_decoder_1_out_2, n4b_decoder_1_out_3, n4b_decoder_1_out_4, n4b_decoder_1_out_5,
       n4b_decoder_1_out_6, n4b_decoder_1_out_7, n4b_decoder_1_out_8, n4b_decoder_1_out_9,
       n4b_decoder_1_out_10, n4b_decoder_1_out_11, n4b_decoder_1_out_12, n4b_decoder_1_out_13,
       n4b_decoder_1_out_14, n4b_decoder_1_out_15, n4b_decoder_1_out_16, n4b_decoder_1_out_17,
       n4b_decoder_2_out_2, n4b_decoder_2_out_3, n4b_decoder_2_out_4, n4b_decoder_2_out_5,
       n4b_decoder_2_out_6, n4b_decoder_2_out_7, n4b_decoder_2_out_8, n4b_decoder_2_out_9,
       n4b_decoder_2_out_10, n4b_decoder_2_out_11, n4b_decoder_2_out_12, n4b_decoder_2_out_13,
       n4b_decoder_2_out_14, n4b_decoder_2_out_15, n4b_decoder_2_out_16, n4b_decoder_2_out_17, or_1_out,
       or_2_out, or_3_out, or_4_out, or_5_out, or_6_out, or_7_out, or_8_out, or_9_out, or_10_out, or_11_out,
       or_12_out, or_13_out, or_14_out, or_15_out, or_16_out, or_17_out, undriven;

  or or_1 (or_1_out, n4b_decoder_2_out_3, or_2_out, or_3_out);
  and and_1 (IP_Read, or_1_out, Clock);
  buf or_2 (or_2_out, 1'b0);  // OR_Gate
  _4b_decoder u_4b_decoder_1 (
    .data(Instruction), .out_2(n4b_decoder_1_out_2), .out_3(n4b_decoder_1_out_3),
    .out_4(n4b_decoder_1_out_4), .out_5(n4b_decoder_1_out_5), .out_6(n4b_decoder_1_out_6),
    .out_7(n4b_decoder_1_out_7), .out_8(n4b_decoder_1_out_8), .out_9(n4b_decoder_1_out_9),
    .out_10(n4b_decoder_1_out_10), .out_11(n4b_decoder_1_out_11), .out_12(n4b_decoder_1_out_12),
    .out_13(n4b_decoder_1_out_13), .out_14(n4b_decoder_1_out_14), .out_15(n4b_decoder_1_out_15),
    .out_16(n4b_decoder_1_out_16), .out_17(n4b_decoder_1_out_17));
  buf or_3 (or_3_out, 1'b0);  // OR_Gate
  and and_2 (Memory_Read, or_4_out, Clock);
  or or_4 (or_4_out, n4b_decoder_2_out_3, or_5_out, or_6_out);
  buf or_5 (or_5_out, 1'b0);  // OR_Gate
  buf or_6 (or_6_out, 1'b0);  // OR_Gate
  and and_3 (Instruction_reg__Write, n4b_decoder_2_out_3, Clock);
  and and_4 (and_4_out, n4b_decoder_2_out_5, n4b_decoder_1_out_2);
  and and_5 (IP_Increase, or_7_out, Clock);
  or or_7 (or_7_out, n4b_decoder_2_out_4, or_8_out, or_9_out);
  buf or_8 (or_8_out, 1'b0);  // OR_Gate
  buf or_9 (or_9_out, 1'b0);  // OR_Gate
  buf or_10 (or_10_out, 1'b0);  // OR_Gate
  and and_6 (\µIC_Clear , or_10_out, Clock);
  and and_7 (IParam1_Write, or_11_out, Clock);
  buf or_11 (or_11_out, 1'b0);  // OR_Gate
  _4b_decoder u_4b_decoder_2 (
    .data(\µ_Instruction_Counter ), .out_2(n4b_decoder_2_out_2), .out_3(n4b_decoder_2_out_3),
    .out_4(n4b_decoder_2_out_4), .out_5(n4b_decoder_2_out_5), .out_6(n4b_decoder_2_out_6),
    .out_7(n4b_decoder_2_out_7), .out_8(n4b_decoder_2_out_8), .out_9(n4b_decoder_2_out_9),
    .out_10(n4b_decoder_2_out_10), .out_11(n4b_decoder_2_out_11), .out_12(n4b_decoder_2_out_12),
    .out_13(n4b_decoder_2_out_13), .out_14(n4b_decoder_2_out_14), .out_15(n4b_decoder_2_out_15),
    .out_16(n4b_decoder_2_out_16), .out_17(n4b_decoder_2_out_17));
  and and_8 (IParam2_Write, or_12_out, Clock);
  buf or_12 (or_12_out, 1'b0);  // OR_Gate
  and and_9 (IParam3_Write, or_13_out, Clock);
  buf or_13 (or_13_out, 1'b0);  // OR_Gate
  buf or_14 (or_14_out, 1'b0);  // OR_Gate
  and and_10 (IParam1_Read, or_14_out, Clock);
  and and_11 (IParam2_Read, or_15_out, Clock);
  buf or_15 (or_15_out, 1'b0);  // OR_Gate
  and and_12 (IParam3_Read, or_16_out, Clock);
  buf or_16 (or_16_out, 1'b0);  // OR_Gate
  and and_13 (WREG_Write, or_17_out, Clock);
  buf or_17 (or_17_out, 1'b0);  // OR_Gate
  and and_14 (Memory_Write, undriven, Clock);

  // Notes on the sheet:
  //   Memory_Write: pull=down
  //   Memory_Read: pull=down
  //   IParam3_Write: pull=down
  //   IP_Read: pull=down
  //   IParam1_Read: pull=down
  //   IParam1_Write: pull=down
  //   Clock: pull=down
  //   WREG_Write: pull=down
  //   IP_Increase: pull=down
  //   Instruction_reg__Write: pull=down
  //   µIC_Clear: pull=down
  //   IParam3_Read: pull=down
  //   IParam2_Write: pull=down
  //   IParam2_Read: pull=down
  //   Instruction: pull=down
  //   µ_Instruction_Counter: pull=down
endmodule

module Processor_V2 (
  input  IN01_8,
  input  IN01_4,
  input  IN01_2,
  input  IN01_1,
  input  IN02_8,
  input  IN02_4,
  input  IN02_2,
  input  IN02_1,
  input  IN03_8,
  input  IN03_4,
  input  IN03_2,
  input  IN03_1,
  input  IN04_8,
  input  IN04_4,
  input  IN04_2,
  input  IN04_1,
  input  IN05_8,
  input  IN05_4,
  input  IN05_2,
  input  IN05_1,
  input  IN06_8,
  input  IN06_4,
  input  IN06_2,
  input  IN06_1,
  input  IN07_8,
  input  IN07_4,
  input  IN07_2,
  input  IN07_1,
  input  IN08_8,
  input  IN08_4,
  input  IN08_2,
  input  IN08_1,
  input  RESET,
  input  Inc_Program_Address,
  input  Decrease_Program_Address,
  input  Reset_Program_Address,
  input  Write_Program_Data,
  input  Program,
  input  PD8,
  input  PD4,
  input  PD2,
  input  PD1,
  output OUT01_1,
  output OUT01_2,
  output OUT01_4,
  output OUT01_8,
  output OUT02_1,
  output OUT02_2,
  output OUT02_4,
  output OUT02_8,
  output OUT03_1,
  output OUT03_2,
  output OUT03_4,
  output OUT03_8,
  output OUT04_1,
  output OUT04_2,
  output OUT04_4,
  output OUT04_8,
  output OUT05_1,
  output OUT05_2,
  output OUT05_4,
  output OUT05_8,
  output OUT06_1,
  output OUT06_2,
  output OUT06_4,
  output OUT06_8,
  output OUT07_1,
  output OUT07_2,
  output OUT07_4,
  output OUT07_8,
  output OUT08_1,
  output OUT08_2,
  output OUT08_4,
  output OUT08_8
);

  wire alu_v2_1_carry_flag, alu_v2_1_zero_flag, input_pin_logic_v2_1_read, pull_resistor_5_node,
       pull_resistor_6_node, pull_resistor_7_node, pull_resistor_8_node, pull_resistor_9_node,
       pull_resistor_10_node, pull_resistor_11_node, pull_resistor_12_node, pull_resistor_13_node,
       pull_resistor_14_node, pull_resistor_15_node, pull_resistor_16_node, pull_resistor_17_node,
       pull_resistor_18_node, pull_resistor_19_node, pull_resistor_21_node, pull_resistor_22_node,
       pull_resistor_24_node, pull_resistor_25_node, pull_resistor_26_node, pull_resistor_29_node,
       pull_resistor_30_node, pull_resistor_31_node, ram_v2_1_out_1, ram_v2_1_out_2, ram_v2_1_out_4,
       ram_v2_1_out_8;

  RAM_V2 ram_v2_1 (
    .Address_1(pull_resistor_17_node), .Address_2(pull_resistor_15_node), .Address_4(pull_resistor_14_node),
    .Address_8(pull_resistor_13_node), .Address_16(pull_resistor_9_node), .Address_32(pull_resistor_11_node),
    .Address_64(pull_resistor_8_node), .Address_128(pull_resistor_10_node),
    .Address_256(pull_resistor_12_node), .Address_512(pull_resistor_7_node),
    .Address_1024(pull_resistor_6_node), .Address_2048(pull_resistor_5_node), .In_1(ram_v2_1_out_1),
    .In_2(ram_v2_1_out_2), .In_4(ram_v2_1_out_4), .In_8(ram_v2_1_out_8), .Out_1(ram_v2_1_out_1),
    .Out_2(ram_v2_1_out_2), .Out_4(ram_v2_1_out_4), .Out_8(ram_v2_1_out_8), .Read(pull_resistor_25_node),
    .Write(pull_resistor_16_node));
  ALU_V2 alu_v2_1 (
    .In_1(ram_v2_1_out_1), .In_2(ram_v2_1_out_2), .In_4(ram_v2_1_out_4), .In_8(ram_v2_1_out_8),
    .Out_1(ram_v2_1_out_1), .Out_2(ram_v2_1_out_2), .Out_4(ram_v2_1_out_4), .Out_8(ram_v2_1_out_8),
    .WREG_Write(pull_resistor_30_node), .WREG_Read(pull_resistor_21_node),
    .Operation_1(pull_resistor_22_node), .Operation_2(pull_resistor_24_node),
    .Operation_4(pull_resistor_19_node), .Output_Read(pull_resistor_18_node),
    .Carry_Flag(alu_v2_1_carry_flag), .Zero_Flag(alu_v2_1_zero_flag));
  Input_Pin_Logic_V2 input_pin_logic_v2_1 (
    .IN01_8(IN01_8), .IN01_4(IN01_4), .IN01_2(IN01_2), .IN01_1(IN01_1), .IN02_8(IN02_8), .IN02_4(IN02_4),
    .IN02_2(IN02_2), .IN02_1(IN02_1), .IN03_8(IN03_8), .IN03_4(IN03_4), .IN03_2(IN03_2), .IN03_1(IN03_1),
    .IN04_8(IN04_8), .IN04_4(IN04_4), .IN04_2(IN04_2), .IN04_1(IN04_1), .IN05_8(IN05_8), .IN05_4(IN05_4),
    .IN05_2(IN05_2), .IN05_1(IN05_1), .IN06_8(IN06_8), .IN06_4(IN06_4), .IN06_2(IN06_2), .IN06_1(IN06_1),
    .IN07_8(IN07_8), .IN07_4(IN07_4), .IN07_2(IN07_2), .IN07_1(IN07_1), .IN08_8(IN08_8), .IN08_4(IN08_4),
    .IN08_2(IN08_2), .IN08_1(IN08_1), .Address_1(pull_resistor_17_node), .Address_2(pull_resistor_15_node),
    .Address_4(pull_resistor_14_node), .Address_8(pull_resistor_13_node), .Out_1(ram_v2_1_out_1),
    .Out_2(ram_v2_1_out_2), .Out_4(ram_v2_1_out_4), .Out_8(ram_v2_1_out_8), .Read(input_pin_logic_v2_1_read));
  Pull_Resistor pull_resistor_1 (.node(ram_v2_1_out_4));
  Pull_Resistor pull_resistor_2 (.node(ram_v2_1_out_8));
  Pull_Resistor pull_resistor_3 (.node(ram_v2_1_out_1));
  Pull_Resistor pull_resistor_4 (.node(ram_v2_1_out_2));
  Pull_Resistor pull_resistor_5 (.node(pull_resistor_5_node));
  Pull_Resistor pull_resistor_6 (.node(pull_resistor_6_node));
  Pull_Resistor pull_resistor_7 (.node(pull_resistor_7_node));
  Pull_Resistor pull_resistor_8 (.node(pull_resistor_8_node));
  Pull_Resistor pull_resistor_9 (.node(pull_resistor_9_node));
  Pull_Resistor pull_resistor_10 (.node(pull_resistor_10_node));
  Pull_Resistor pull_resistor_11 (.node(pull_resistor_11_node));
  Pull_Resistor pull_resistor_12 (.node(pull_resistor_12_node));
  Pull_Resistor pull_resistor_13 (.node(pull_resistor_13_node));
  Pull_Resistor pull_resistor_14 (.node(pull_resistor_14_node));
  Pull_Resistor pull_resistor_15 (.node(pull_resistor_15_node));
  Pull_Resistor pull_resistor_16 (.node(pull_resistor_16_node));
  Pull_Resistor pull_resistor_17 (.node(pull_resistor_17_node));
  Pull_Resistor pull_resistor_18 (.node(pull_resistor_18_node));
  Pull_Resistor pull_resistor_19 (.node(pull_resistor_19_node));
  Pull_Resistor pull_resistor_20 (.node(alu_v2_1_carry_flag));
  Pull_Resistor pull_resistor_21 (.node(pull_resistor_21_node));
  Pull_Resistor pull_resistor_22 (.node(pull_resistor_22_node));
  Pull_Resistor pull_resistor_23 (.node(alu_v2_1_zero_flag));
  Pull_Resistor pull_resistor_24 (.node(pull_resistor_24_node));
  Pull_Resistor pull_resistor_25 (.node(pull_resistor_25_node));
  Pull_Resistor pull_resistor_26 (.node(pull_resistor_26_node));
  Pull_Resistor pull_resistor_27 (.node(RESET));
  Pull_Resistor pull_resistor_28 (.node(input_pin_logic_v2_1_read));
  Pull_Resistor pull_resistor_29 (.node(pull_resistor_29_node));
  Pull_Resistor pull_resistor_30 (.node(pull_resistor_30_node));
  Pull_Resistor pull_resistor_31 (.node(pull_resistor_31_node));
  Output_Pin_Logic_V2 output_pin_logic_v2_1 (
    .Address_1(pull_resistor_17_node), .Address_2(pull_resistor_15_node), .Address_4(pull_resistor_14_node),
    .Address_8(pull_resistor_13_node), .In_1(ram_v2_1_out_1), .In_2(ram_v2_1_out_2), .In_4(ram_v2_1_out_4),
    .In_8(ram_v2_1_out_8), .Write(pull_resistor_29_node), .OUT01_1(OUT01_1), .OUT01_2(OUT01_2),
    .OUT01_4(OUT01_4), .OUT01_8(OUT01_8), .OUT02_1(OUT02_1), .OUT02_2(OUT02_2), .OUT02_4(OUT02_4),
    .OUT02_8(OUT02_8), .OUT03_1(OUT03_1), .OUT03_2(OUT03_2), .OUT03_4(OUT03_4), .OUT03_8(OUT03_8),
    .OUT04_1(OUT04_1), .OUT04_2(OUT04_2), .OUT04_4(OUT04_4), .OUT04_8(OUT04_8), .OUT05_1(OUT05_1),
    .OUT05_2(OUT05_2), .OUT05_4(OUT05_4), .OUT05_8(OUT05_8), .OUT06_1(OUT06_1), .OUT06_2(OUT06_2),
    .OUT06_4(OUT06_4), .OUT06_8(OUT06_8), .OUT07_1(OUT07_1), .OUT07_2(OUT07_2), .OUT07_4(OUT07_4),
    .OUT07_8(OUT07_8), .OUT08_1(OUT08_1), .OUT08_2(OUT08_2), .OUT08_4(OUT08_4), .OUT08_8(OUT08_8));
  Program_Pin_Logic_V2 program_pin_logic_v2_1 (
    .A_1(pull_resistor_17_node), .A_2(pull_resistor_15_node), .A_4(pull_resistor_14_node),
    .A_8(pull_resistor_13_node), .A_16(pull_resistor_9_node), .A_32(pull_resistor_11_node),
    .A_64(pull_resistor_8_node), .A_128(pull_resistor_10_node), .A_256(pull_resistor_12_node),
    .A_512(pull_resistor_7_node), .A_1024(pull_resistor_6_node), .A_2048(pull_resistor_5_node),
    .DO_1(ram_v2_1_out_1), .DO_2(ram_v2_1_out_2), .DO_4(ram_v2_1_out_4), .DO_8(ram_v2_1_out_8),
    .Data_Write(pull_resistor_26_node), .Program_2(pull_resistor_31_node),
    .Increase_Program_Address(Inc_Program_Address), .Decrease_Program_Address(Decrease_Program_Address),
    .Reset_Program_Address(Reset_Program_Address), .Write_Program_Data(Write_Program_Data),
    .Program(Program), .PD8(PD8), .PD4(PD4), .PD2(PD2), .PD1(PD1));
  CPU_V2 cpu_v2_1 ();  // open: OPLU_Write, IPLU_Read, Reset, PPLU_D_Write, PPLU_Program, WREG_Write, WREG_Read, ALU_OP_1, ALU_OP_2, ALU_OP_4, ALU_Out_Read, Carry_In, Zero_In, RAM_Read, RAM_Write, Clock, in_1

  // Notes on the sheet:
  //   IN05_1: pull=down
  //   OUT01_4: pull=down
  //   OUT04_1: pull=down
  //   OUT08_2: pull=down
  //   Inc_Program_Address: pull=down
  //   IN03_1: pull=down
  //   IN04_1: pull=down
  //   OUT02_8: pull=down
  //   IN05_4: pull=down
  //   OUT01_1: pull=down
  //   IN05_8: pull=down
  //   OUT08_4: pull=down
  //   OUT03_1: pull=down
  //   IN04_2: pull=down
  //   OUT04_4: pull=down
  //   IN01_2: pull=down
  //   IN07_2: pull=down
  //   PD4: pull=down
  //   IN01_8: pull=down
  //   OUT06_1: pull=down
  //   IN02_2: pull=down
  //   IN08_8: pull=down
  //   IN06_1: pull=down
  //   IN08_4: pull=down
  //   Decrease_Program_Address: pull=down
  //   IN03_8: pull=down
  //   OUT03_8: pull=down
  //   OUT07_8: pull=down
  //   OUT01_2: pull=down
  //   OUT05_2: pull=down
  //   IN07_4: pull=down
  //   PD8: pull=down
  //   OUT07_4: pull=down
  //   IN01_4: pull=down
  //   Reset_Program_Address: pull=down
  //   IN08_1: pull=down
  //   OUT04_8: pull=down
  //   OUT03_4: pull=down
  //   Program: pull=down
  //   IN05_2: pull=down
  //   OUT08_8: pull=down
  //   IN06_4: pull=down
  //   IN02_1: pull=down
  //   IN04_4: pull=down
  //   OUT02_2: pull=down
  //   IN07_8: pull=down
  //   OUT05_1: pull=down
  //   IN01_1: pull=down
  //   PD2: pull=down
  //   IN03_2: pull=down
  //   OUT02_1: pull=down
  //   OUT06_8: pull=down
  //   OUT08_1: pull=down
  //   PD1: pull=down
  //   OUT06_2: pull=down
  //   OUT06_4: pull=down
  //   IN07_1: pull=down
  //   OUT05_4: pull=down
  //   RESET: pull=down
  //   IN02_8: pull=down
  //   IN08_2: pull=down
  //   OUT07_1: pull=down
  //   OUT02_4: pull=down
  //   IN03_4: pull=down
  //   IN02_4: pull=down
  //   OUT03_2: pull=down
  //   Write_Program_Data: pull=down
  //   IN04_8: pull=down
  //   OUT04_2: pull=down
  //   IN06_2: pull=down
  //   IN06_8: pull=down
  //   OUT05_8: pull=down
  //   OUT07_2: pull=down
  //   OUT01_8: pull=down
  //   DATA BUS
  //   ADDRESS BUS
  //   INSTRUCTION BUS
endmodule

// CPU
module CPU_V2 (
  input  in_1,
  input  Reset,
  input  PPLU_D_Write,
  input  PPLU_Program,
  input  Carry_In,
  input  Zero_In,
  input  Clock,
  output OPLU_Write,
  output IPLU_Read,
  output WREG_Write,
  output WREG_Read,
  output ALU_OP_1,
  output ALU_OP_2,
  output ALU_OP_4,
  output ALU_Out_Read,
  output RAM_Read,
  output RAM_Write
);

  wire or_1_out, or_2_out, undriven, undriven_3, undriven_4, xor_1_out;
  wire [3:0] Instruction_Register_q, undriven_2, \µ_instruction_counter_1_q ;
  wire [11:0] Instruction_Param_3_q, IP_REG_adress_for_ram, register_12b_1_q;

  IP_Register IP_REG (
    .DATA(register_12b_1_q), .ADRESS_FOR_RAM(IP_REG_adress_for_ram));  // open: SAVE, INC, DEC, Read, RESET
  register_12b register_12b_1 (.Data(IP_REG_adress_for_ram), .Read(1'b1), .Q(register_12b_1_q));  // open: Write, Clear
  register Instruction_Param_3 (.Data(undriven_2), .Q(Instruction_Param_3_q[3:0]));  // open: Write, Clear, Read
  register Instruction_Param_2 (.Data(undriven_2), .Q(Instruction_Param_3_q[7:4]));  // open: Write, Clear, Read
  register Intruction_Param_1 (.Data(undriven_2), .Q(Instruction_Param_3_q[11:8]));  // open: Write, Clear, Read
  register Instruction_Register (.Write(undriven), .Read(1'b1), .Q(Instruction_Register_q));  // open: Data, Clear
  instruction_decoder instruction_decoder_1 ();  // open: Instruction, IP_Read, Memory_Read, Instruction_reg__Write, IP_Increase, IParam1_Write, IParam2_Write, IParam3_Write, IParam1_Read, IParam2_Read, IParam3_Read, WREG_Write, Memory_Write, µIC_Clear, µ_Instruction_Counter, Clock
  Hex_Digit_Display hex_digit_display_1 (.value(\µ_instruction_counter_1_q ));  // open: dp
  \µ_Instruction_Counter  \u_µ_instruction_counter_1  (
    .Increase(or_1_out), .Clear(or_2_out), .Q(\µ_instruction_counter_1_q ));
  or or_1 (or_1_out, Clock, xor_1_out);
  or or_2 (or_2_out, undriven_3, undriven_4);
  buf xor_1 (xor_1_out, undriven_4);  // XOR_Gate

  // Notes on the sheet:
  //   ALU_OP_1: pull=down
  //   WREG_Read: pull=down
  //   Reset: pull=down
  //   WREG_Write: pull=down
  //   in_1: pull=down
  //   PPLU_D_Write: pull=down
  //   ALU_OP_2: pull=down
  //   ALU_Out_Read: pull=down
  //   ALU_OP_4: pull=down
  //   OPLU_Write: pull=down
  //   Clock: pull=down
  //   PPLU_Program: pull=down
  //   IPLU_Read: pull=down
  //   Carry_In: pull=down
  //   RAM_Write: pull=down
  //   Zero_In: pull=down
  //   RAM_Read: pull=down
  //   0000 - NOP
  //   0001 XXXX XXXX XXXX - MOVRW
  //   0010 XXXX XXXX XXXX - MOVWR
  //   0011 XXXX - MOVWO
  //   0100 XXXX - MOVIW
  //   0101 XXXX XXXX XXXX - JMP
endmodule

// ALU
module ALU_V2 (
  input  In_1,
  input  In_2,
  input  In_4,
  input  In_8,
  input  WREG_Write,
  input  WREG_Read,
  input  Operation_1,
  input  Operation_2,
  input  Operation_4,
  input  Output_Read,
  output Out_1,
  output Out_2,
  output Out_4,
  output Out_8,
  output Carry_Flag,
  output Zero_Flag
);

  wire adder_1_cout, and_1_out, and_2_out, and_3_out, and_5_out, and_6_out, and_7_out, and_8_out, and_9_out,
       or_1_out, or_2_out;
  wire [3:0] adder_1_out, nand_1_out, nor_1_out, outputter_1_out, outputter_5_out, WREG_q, xor_1_out,
       xor_2_out;
  wire [3:3] and_4_out;

  register WREG (.Data({In_8, In_4, In_2, In_1}), .Write(WREG_Write), .Clear(1'b0), .Read(1'b1), .Q(WREG_q));
  outputter MOVWR (.In(WREG_q), .Read(WREG_Read), .Out({Out_8, Out_4, Out_2, Out_1}));
  register Buffer (
    .Data(outputter_1_out), .Write(or_2_out), .Clear(1'b0), .Read(Output_Read),
    .Q({Out_8, Out_4, Out_2, Out_1}));
  assign xor_1_out = {In_8, In_4, In_2, In_1} ^ {4{and_4_out[3]}};  // XOR_Gate xor_1, 4 bits wide
  Adder #(.width(4)) adder_1 (.a(WREG_q), .b(xor_1_out), .out(adder_1_out), .cin(and_4_out[3]), .cout(adder_1_cout));
  assign nor_1_out = ~(WREG_q | {In_8, In_4, In_2, In_1});  // NOR_Gate nor_1, 4 bits wide
  assign xor_2_out = WREG_q ^ {In_8, In_4, In_2, In_1};  // XOR_Gate xor_2, 4 bits wide
  assign nand_1_out = ~(WREG_q & {In_8, In_4, In_2, In_1});  // NAND_Gate nand_1, 4 bits wide
  or or_1 (or_1_out, and_4_out[3], and_3_out);
  outputter outputter_1 (.In(adder_1_out), .Read(or_1_out), .Out(outputter_1_out));
  D_Flip_Flop #(.trigger("high")) d_ff_1 (
    .clk(or_2_out), .D(adder_1_cout), .Q(Carry_Flag), .preset(1'b0), .en(1'b1), .reset(1'b0));  // open: Qn
  outputter outputter_2 (.In(nor_1_out), .Read(and_5_out), .Out(outputter_1_out));
  outputter outputter_3 (.In(xor_2_out), .Read(and_6_out), .Out(outputter_1_out));
  outputter outputter_4 (.In(nand_1_out), .Read(and_7_out), .Out(outputter_1_out));
  outputter outputter_5 (.In(outputter_1_out), .Read(1'b1), .Out(outputter_5_out));
  and and_1 (and_1_out, ~outputter_5_out[3], ~outputter_5_out[2], ~outputter_5_out[1], ~outputter_5_out[0]);  // AND_Gate
  D_Flip_Flop #(.trigger("high")) d_ff_2 (
    .clk(and_1_out), .Q(Zero_Flag), .preset(1'b0), .en(1'b1), .reset(1'b0));  // open: D, Qn
  or or_2 (or_2_out, and_3_out, and_4_out[3], and_5_out, and_6_out, and_7_out);
  and and_2 (and_2_out, ~Operation_1, ~Operation_2, ~Operation_4);  // AND_Gate
  and and_3 (and_3_out, Operation_1, ~Operation_2, ~Operation_4);  // AND_Gate
  and and_4 (and_4_out[3], ~Operation_1, Operation_2, ~Operation_4);  // AND_Gate
  and and_5 (and_5_out, Operation_1, Operation_2, ~Operation_4);  // AND_Gate
  and and_6 (and_6_out, ~Operation_1, ~Operation_2, Operation_4);  // AND_Gate
  and and_7 (and_7_out, Operation_1, ~Operation_2, Operation_4);  // AND_Gate
  and and_8 (and_8_out, ~Operation_1, Operation_2, Operation_4);  // AND_Gate
  and and_9 (and_9_out, Operation_1, Operation_2, Operation_4);

  // Notes on the sheet:
  //   In_4: pull=down
  //   Operation_4: pull=down
  //   Out_8: pull=down
  //   In_2: pull=down
  //   In_8: pull=down
  //   Operation_2: pull=down
  //   Out_2: pull=down
  //   Operation_1: pull=down
  //   Output_Read: pull=down
  //   Out_4: pull=down
  //   WREG_Write: pull=down
  //   Out_1: pull=down
  //   WREG_Read: pull=down
  //   In_1: pull=down
  //   001 - Add
  //   011 - Nor
  //   100 - Xor
  //   000 - No Operation
  //   010 - Subtract
  //   101 - Nand
endmodule

// RAM
module RAM_V2 (
  input  Address_1,
  input  Address_2,
  input  Address_4,
  input  Address_8,
  input  Address_16,
  input  Address_32,
  input  Address_64,
  input  Address_128,
  input  Address_256,
  input  Address_512,
  input  Address_1024,
  input  Address_2048,
  input  In_1,
  input  In_2,
  input  In_4,
  input  In_8,
  input  Read,
  input  Write,
  output Out_1,
  output Out_2,
  output Out_4,
  output Out_8
);

  wire or_1_out;

  or or_1 (or_1_out, Write, Read);
  RAM #(.addrWidth(12), .dataWidth(4), .bus("asynch")) ram_1 (
    .addr({Address_2048, Address_1024, Address_512, Address_256, Address_128, Address_64, Address_32, Address_16, Address_8, Address_4, Address_2, Address_1}),
    .data({In_8, In_4, In_2, In_1}), .sel(or_1_out), .ld(Read), .clr(1'b0));

  assign Out_1 = In_1;
  assign Out_2 = In_2;
  assign Out_4 = In_4;
  assign Out_8 = In_8;

  // Notes on the sheet:
  //   In_2: pull=down
  //   In_4: pull=down
  //   Address_128: pull=down
  //   Read: pull=down
  //   Address_16: pull=down
  //   Write: pull=down
  //   Address_2: pull=down
  //   Address_64: pull=down
  //   Address_8: pull=down
  //   Address_1024: pull=down
  //   Address_1: pull=down
  //   In_1: pull=down
  //   Out_2: pull=down
  //   Out_1: pull=down
  //   Address_32: pull=down
  //   Address_2048: pull=down
  //   Address_4: pull=down
  //   In_8: pull=down
  //   Address_512: pull=down
  //   Address_256: pull=down
  //   Out_4: pull=down
  //   Out_8: pull=down
endmodule

// PPLU
module Program_Pin_Logic_V2 (
  input  Increase_Program_Address,
  input  Decrease_Program_Address,
  input  Reset_Program_Address,
  input  Write_Program_Data,
  input  Program,
  input  PD8,
  input  PD4,
  input  PD2,
  input  PD1,
  output A_1,
  output A_2,
  output A_4,
  output A_8,
  output A_16,
  output A_32,
  output A_64,
  output A_128,
  output A_256,
  output A_512,
  output A_1024,
  output A_2048,
  output DO_1,
  output DO_2,
  output DO_4,
  output DO_8,
  output Data_Write,
  output Program_2
);

  wire and_1_out, Program_IP_REG_p5, Program_IP_REG_p7;

  and and_1 (and_1_out, Increase_Program_Address, Program);
  // IP_Register Program_IP_REG: pin names not known; wires that end beside it: 1'b0, {A_2048, A_1024, A_512, A_256, A_128, A_64, A_32, A_16, A_8, A_4, A_2, A_1}, 1'b0, and_1_out, Program_IP_REG_p5, Program, Program_IP_REG_p7
  and and_2 (Program_IP_REG_p5, Decrease_Program_Address, Program);
  and and_3 (Program_IP_REG_p7, Reset_Program_Address, Program);
  and and_4 (Data_Write, Write_Program_Data, Program);
  outputter outputter_1 (.In({PD8, PD4, PD2, PD1}), .Read(Program), .Out({DO_8, DO_4, DO_2, DO_1}));

  assign Program_2 = Program;

  // Notes on the sheet:
  //   A_32: pull=down
  //   Reset_Program_Address: pull=down
  //   Decrease_Program_Address: pull=down
  //   Write_Program_Data: pull=down
  //   Increase_Program_Address: pull=down
  //   A_256: pull=down
  //   A_2048: pull=down
  //   DO_8: pull=down
  //   PD4: pull=down
  //   A_64: pull=down
  //   A_1024: pull=down
  //   PD1: pull=down
  //   A_2: pull=down
  //   A_4: pull=down
  //   DO_2: pull=down
  //   A_512: pull=down
  //   DO_1: pull=down
  //   A_1: pull=down
  //   A_128: pull=down
  //   A_16: pull=down
  //   Program_2: pull=down
  //   Program: pull=down
  //   A_8: pull=down
  //   PD8: pull=down
  //   Data_Write: pull=down
  //   PD2: pull=down
  //   DO_4: pull=down
endmodule

// IPLU
module Input_Pin_Logic_V2 (
  input  Address_1,
  input  Address_2,
  input  Address_4,
  input  Address_8,
  input  IN01_8,
  input  IN01_4,
  input  IN01_2,
  input  IN01_1,
  input  IN02_8,
  input  IN02_4,
  input  IN02_2,
  input  IN02_1,
  input  IN03_8,
  input  IN03_4,
  input  IN03_2,
  input  IN03_1,
  input  IN04_8,
  input  IN04_4,
  input  IN04_2,
  input  IN04_1,
  input  IN05_8,
  input  IN05_4,
  input  IN05_2,
  input  IN05_1,
  input  IN06_8,
  input  IN06_4,
  input  IN06_2,
  input  IN06_1,
  input  IN07_8,
  input  IN07_4,
  input  IN07_2,
  input  IN07_1,
  input  IN08_8,
  input  IN08_4,
  input  IN08_2,
  input  IN08_1,
  output Out_1,
  output Out_2,
  output Out_4,
  output Out_8,
  output Read
);

  wire and_1_out, and_2_out, and_3_out, and_4_out, and_5_out, and_6_out, and_7_out, and_8_out;
  wire [3:0] outputter_1_out;

  outputter outputter_1 (.In({IN01_8, IN01_4, IN01_2, IN01_1}), .Read(and_8_out), .Out(outputter_1_out));
  outputter outputter_2 (.In({IN02_8, IN02_4, IN02_2, IN02_1}), .Read(and_7_out), .Out(outputter_1_out));
  outputter outputter_3 (.In({IN03_8, IN03_4, IN03_2, IN03_1}), .Read(and_6_out), .Out(outputter_1_out));
  outputter outputter_4 (.In({IN04_8, IN04_4, IN04_2, IN04_1}), .Read(and_4_out), .Out(outputter_1_out));
  outputter outputter_5 (.In({IN05_8, IN05_4, IN05_2, IN05_1}), .Read(and_5_out), .Out(outputter_1_out));
  outputter outputter_6 (.In({IN06_8, IN06_4, IN06_2, IN06_1}), .Read(and_3_out), .Out(outputter_1_out));
  outputter outputter_7 (.In({IN07_8, IN07_4, IN07_2, IN07_1}), .Read(and_2_out));  // open: Out
  outputter outputter_8 (.In({IN08_8, IN08_4, IN08_2, IN08_1}), .Read(and_1_out), .Out(outputter_1_out));
  and and_1 (and_1_out, ~Address_8, Address_4, Address_2, Address_1);  // AND_Gate
  and and_2 (and_2_out, ~Address_8, Address_4, Address_2, ~Address_1);  // AND_Gate
  outputter outputter_9 (.In(outputter_1_out), .Read(Read), .Out({Out_8, Out_4, Out_2, Out_1}));
  and and_3 (and_3_out, ~Address_8, Address_4, ~Address_2, Address_1);  // AND_Gate
  and and_4 (and_4_out, ~Address_8, ~Address_4, Address_2, Address_1);  // AND_Gate
  and and_5 (and_5_out, ~Address_8, Address_4, ~Address_2, ~Address_1);  // AND_Gate
  and and_6 (and_6_out, ~Address_8, ~Address_4, Address_2, ~Address_1);  // AND_Gate
  and and_7 (and_7_out, ~Address_8, ~Address_4, ~Address_2, Address_1);  // AND_Gate
  and and_8 (and_8_out, ~Address_8, ~Address_4, ~Address_2, ~Address_1);  // AND_Gate

  // Notes on the sheet:
  //   IN07_1: pull=down
  //   IN04_2: pull=down
  //   IN07_8: pull=down
  //   IN07_2: pull=down
  //   IN05_2: pull=down
  //   IN01_4: pull=down
  //   IN02_1: pull=down
  //   IN03_1: pull=down
  //   Address_2: pull=down
  //   Out_1: pull=down
  //   IN06_2: pull=down
  //   Out_8: pull=down
  //   Address_8: pull=down
  //   IN01_1: pull=down
  //   IN05_4: pull=down
  //   IN02_2: pull=down
  //   IN04_8: pull=down
  //   IN07_4: pull=down
  //   IN08_8: pull=down
  //   IN05_1: pull=down
  //   IN03_8: pull=down
  //   IN08_1: pull=down
  //   IN02_4: pull=down
  //   IN02_8: pull=down
  //   Read: pull=down
  //   Out_2: pull=down
  //   IN03_2: pull=down
  //   IN06_8: pull=down
  //   IN01_2: pull=down
  //   IN01_8: pull=down
  //   IN04_1: pull=down
  //   IN08_2: pull=down
  //   IN04_4: pull=down
  //   IN03_4: pull=down
  //   Address_4: pull=down
  //   IN08_4: pull=down
  //   IN06_4: pull=down
  //   Address_1: pull=down
  //   IN06_1: pull=down
  //   Out_4: pull=down
  //   IN05_8: pull=down
endmodule

// OPLU
module Output_Pin_Logic_V2 (
  input  Address_1,
  input  Address_2,
  input  Address_4,
  input  Address_8,
  input  In_1,
  input  In_2,
  input  In_4,
  input  In_8,
  input  Write,
  output OUT01_1,
  output OUT01_2,
  output OUT01_4,
  output OUT01_8,
  output OUT02_1,
  output OUT02_2,
  output OUT02_4,
  output OUT02_8,
  output OUT03_1,
  output OUT03_2,
  output OUT03_4,
  output OUT03_8,
  output OUT04_1,
  output OUT04_2,
  output OUT04_4,
  output OUT04_8,
  output OUT05_1,
  output OUT05_2,
  output OUT05_4,
  output OUT05_8,
  output OUT06_1,
  output OUT06_2,
  output OUT06_4,
  output OUT06_8,
  output OUT07_1,
  output OUT07_2,
  output OUT07_4,
  output OUT07_8,
  output OUT08_1,
  output OUT08_2,
  output OUT08_4,
  output OUT08_8
);

  wire and_1_out, and_2_out, and_3_out, and_4_out, and_5_out, and_6_out, and_7_out, and_8_out;

  and and_1 (and_1_out, Write, ~Address_8, Address_4, Address_2, ~Address_1);  // AND_Gate
  and and_2 (and_2_out, ~Write, ~Address_8, Address_4, Address_2, Address_1);  // AND_Gate
  and and_3 (and_3_out, Write, ~Address_8, Address_4, ~Address_2, Address_1);  // AND_Gate
  and and_4 (and_4_out, Write, ~Address_8, Address_4, ~Address_2, ~Address_1);  // AND_Gate
  and and_5 (and_5_out, Write, ~Address_8, ~Address_4, Address_2, ~Address_1);  // AND_Gate
  and and_6 (and_6_out, Write, ~Address_8, ~Address_4, Address_2, Address_1);  // AND_Gate
  and and_7 (and_7_out, Write, ~Address_8, ~Address_4, ~Address_2, Address_1);  // AND_Gate
  and and_8 (and_8_out, Write, ~Address_8, ~Address_4, ~Address_2, ~Address_1);  // AND_Gate
  register register_1 (
    .Data({In_8, In_4, In_2, In_1}), .Write(and_8_out), .Clear(1'b0), .Read(1'b1),
    .Q({OUT01_8, OUT01_4, OUT01_2, OUT01_1}));
  register register_2 (
    .Data({In_8, In_4, In_2, In_1}), .Write(and_7_out), .Clear(1'b0), .Read(1'b1),
    .Q({OUT02_8, OUT02_4, OUT02_2, OUT02_1}));
  register register_3 (
    .Data({In_8, In_4, In_2, In_1}), .Write(and_5_out), .Clear(1'b0), .Read(1'b1),
    .Q({OUT03_8, OUT03_4, OUT03_2, OUT03_1}));
  register register_4 (
    .Data({In_8, In_4, In_2, In_1}), .Write(and_6_out), .Clear(1'b0), .Read(1'b1),
    .Q({OUT04_8, OUT04_4, OUT04_2, OUT04_1}));
  register register_5 (
    .Data({In_8, In_4, In_2, In_1}), .Write(and_4_out), .Clear(1'b0), .Read(1'b1),
    .Q({OUT05_8, OUT05_4, OUT05_2, OUT05_1}));
  register register_6 (
    .Data({In_8, In_4, In_2, In_1}), .Write(and_3_out), .Clear(1'b0), .Read(1'b1),
    .Q({OUT06_8, OUT06_4, OUT06_2, OUT06_1}));
  register register_7 (
    .Data({In_8, In_4, In_2, In_1}), .Write(and_1_out), .Clear(1'b0), .Read(1'b1),
    .Q({OUT07_8, OUT07_4, OUT07_2, OUT07_1}));
  register register_8 (
    .Data({In_8, In_4, In_2, In_1}), .Write(and_2_out), .Clear(1'b0), .Read(1'b1),
    .Q({OUT08_8, OUT08_4, OUT08_2, OUT08_1}));

  // Notes on the sheet:
  //   OUT06_4: pull=down
  //   OUT06_2: pull=down
  //   OUT03_8: pull=down
  //   OUT06_8: pull=down
  //   OUT05_1: pull=down
  //   OUT01_2: pull=down
  //   OUT05_4: pull=down
  //   OUT02_4: pull=down
  //   Address_8: pull=down
  //   OUT08_2: pull=down
  //   OUT03_4: pull=down
  //   OUT04_1: pull=down
  //   OUT01_8: pull=down
  //   OUT08_4: pull=down
  //   In_2: pull=down
  //   OUT07_1: pull=down
  //   Address_4: pull=down
  //   In_4: pull=down
  //   Address_2: pull=down
  //   OUT06_1: pull=down
  //   Write: pull=down
  //   OUT04_2: pull=down
  //   OUT03_1: pull=down
  //   OUT01_1: pull=down
  //   OUT03_2: pull=down
  //   Address_1: pull=down
  //   OUT02_8: pull=down
  //   OUT04_8: pull=down
  //   OUT02_2: pull=down
  //   OUT05_2: pull=down
  //   OUT01_4: pull=down
  //   In_1: pull=down
  //   OUT08_1: pull=down
  //   OUT07_2: pull=down
  //   OUT08_8: pull=down
  //   OUT07_8: pull=down
  //   In_8: pull=down
  //   OUT02_1: pull=down
  //   OUT05_8: pull=down
  //   OUT04_4: pull=down
  //   OUT07_4: pull=down
endmodule
